# Fritzing sketch gas_sensor (saved by Fritzing 0.9.3b)
breadboards: 1

parts:
  Part1 = Arduino Uno (Rev3)
  Mod1 = MQ-7 breakout
  R1 = Resistor [tolerance=±5% resistance=220 package=THT]

nets:
  N1: Part1.A0, Mod1.AO
  5V: Part1.5V, Mod1.VCC
  N2: Part1.GND, R1.Pin_1
  N3: Mod1.GND, R1.Pin_0

custom parts:
  MQ-7 breakout: MQ-5 gas sensor
